// Logisim project Cache.circ as structural Verilog: 7 circuits, main circuit main
module main (
  input  EnableTestHalting,
  output [9:0] CorrectCounter,
  output [9:0] HitCounter,
  output [9:0] MissCounter,
  output [9:0] TestNumber,
  output [7:0] ByteRead,
  output [7:0] CorrectByteRead,
  output Halt
);

  wire and_3_out, and_4_out, and_5_out, CLK, CmdIsRead, Correct, CpuRead, CpuWrite, DidContain, HaltTesting,
       MaxItersReached, MemRead, MemWrite, not_1_out, not_2_out, not_4_out, NotDoneTesting, Ok2Count,
       or_1_out, Ready;
  wire [7:0] CpuWriteValue, MemAddress;
  wire [9:0] CpuAddress;
  wire [31:0] Line2Mem, LineFromMem;

  not not_1 (not_1_out, Ready);
  Clock clock_1 (.out(CLK));
  or or_1 (or_1_out, MaxItersReached, Ready);
  Counter #(.width(4), .max('h9)) MaxClocks (
    .load(Ready), .D(4'b0001), .count(not_1_out), .carry(MaxItersReached), .clk(CLK));  // open: Q, clr
  and and_1 (HaltTesting, EnableTestHalting, CmdIsRead, not_2_out);
  not not_2 (not_2_out, Correct);
  not not_3 (NotDoneTesting, Halt);
  Inputs inputs_1 (
    .HaltTesting(HaltTesting), .Ready(or_1_out), .CLK(CLK), .Done(Halt), .Read(CpuRead), .Write(CpuWrite),
    .Address(CpuAddress), .Value(CpuWriteValue), .TestNumber(TestNumber));
  Cache cache_1 (
    .CpuAddress(CpuAddress), .CpuRead(CpuRead), .CpuWrite(CpuWrite), .CpuWriteValue(CpuWriteValue),
    .CLK(CLK), .Ready(Ready), .DidContain(DidContain), .ByteRead(ByteRead), .MemAddress(MemAddress),
    .MemRead(MemRead), .MemWrite(MemWrite), .LineFromMem(LineFromMem), .Line2Mem(Line2Mem));
  // Probe on CpuRead
  // Probe on CpuWrite
  // Probe on CpuAddress
  // Probe on CpuWriteValue
  // Probe on TestNumber
  // Probe on CorrectByteRead
  // Probe on Correct
  // Probe on Ready
  // Probe on DidContain
  // Probe on ByteRead
  // Probe on MemAddress
  // Probe on MemRead
  // Probe on MemWrite
  // Probe on HitCounter
  // Probe on LineFromMem
  // Probe on Line2Mem
  not not_4 (not_4_out, HaltTesting);
  RAM #(.dataWidth(32), .bus("separate")) ram_1 (
    .addr(MemAddress), .din(Line2Mem), .data(LineFromMem), .str(MemWrite), .clk(CLK), .ld(MemRead));  // open: sel, clr
  and and_2 (Ok2Count, Ready, not_4_out, NotDoneTesting);
  and and_3 (and_3_out, Correct, Ok2Count);
  and and_4 (and_4_out, DidContain, Ok2Count);
  and and_5 (and_5_out, MemRead, NotDoneTesting);
  Checker checker_1 (
    .TestNumber(TestNumber), .YourByteRead(ByteRead), .CmdIsRead(CmdIsRead),
    .CorrectByteRead(CorrectByteRead), .Correct(Correct));
  Counter #(.width(10), .max('h3ff)) u_CorrectCounter (
    .count(and_3_out), .Q(CorrectCounter), .clk(CLK));  // open: load, D, carry, clr
  Counter #(.width(10), .max('h3ff)) u_HitCounter (
    .count(and_4_out), .Q(HitCounter), .clk(CLK));  // open: load, D, carry, clr
  Counter #(.width(10), .max('h3ff)) u_MissCounter (
    .count(and_5_out), .Q(MissCounter), .clk(CLK));  // open: load, D, carry, clr
  // Probe on CorrectCounter
  // Probe on HitCounter
  // Probe on MissCounter

  // Other names for the same wires on the sheet: DoneTesting = Halt

  // Notes on the sheet:
  //   Your Answer Inside Here
endmodule

module Cache (
  input  [9:0] CpuAddress,
  input  CpuRead,
  input  CpuWrite,
  input  [7:0] CpuWriteValue,
  input  CLK,
  input  [31:0] LineFromMem,
  output Ready,
  output DidContain,
  output [7:0] ByteRead,
  output [7:0] MemAddress,
  output MemRead,
  output MemWrite,
  output [31:0] Line2Mem
);

  wire ReadFromSet0, ReadFromSet1, WriteToSet0, WriteToSet1;
  wire [1:0] OffsetToSet0, OffsetToSet1;
  wire [6:0] TagToSet0, TagToSet1;

  Demultiplexer #(.width(7), .enable("false")) demultiplexer_1 (
    .out0(TagToSet0), .out1(TagToSet1), .in(CpuAddress[9:3]), .sel(CpuAddress[2]));
  Demultiplexer #(.width(2), .enable("false")) demultiplexer_2 (
    .out0(OffsetToSet0), .out1(OffsetToSet1), .in(CpuAddress[1:0]), .sel(CpuAddress[2]));
  Demultiplexer #(.enable("false")) demultiplexer_3 (
    .out0(ReadFromSet0), .out1(ReadFromSet1), .in(CpuRead), .sel(CpuAddress[2]));
  Demultiplexer #(.enable("false")) demultiplexer_4 (
    .out0(WriteToSet0), .out1(WriteToSet1), .in(CpuWrite), .sel(CpuAddress[2]));
  Set Set0 (.Tag(TagToSet0), .Offset(OffsetToSet0), .CLK(CLK), .Read(ReadFromSet0), .Write(WriteToSet0));
  Set Set1 (.Tag(TagToSet1), .Offset(OffsetToSet1), .CLK(CLK), .Read(ReadFromSet1), .Write(WriteToSet1));

  // Other names for the same wires on the sheet: Set = CpuAddress[2]; Offset[1:0] = CpuAddress[1:0];
  //   Tag[6:0] = CpuAddress[9:3]

  // Notes on the sheet:
  //   Address Bits = 10
  //   (1) Split CPU Address
  //   Line Size = 4
  //   Get coordinates to look inside cache
  //   W = 3
  //   (2) Using Set: feed the Offset, Tag, CpuRead, and CpuWrite to the right set
  //   Num Sets = 2
  //   C =4*3*2 = 24bytes
  //   Tag bits = 7
endmodule

module Inputs (
  input  HaltTesting,
  input  Ready,
  input  CLK,
  output Done,
  output Read,
  output Write,
  output [9:0] Address,
  output [7:0] Value,
  output [9:0] TestNumber
);

  wire and_1_out, not_1_out, not_2_out;

  not not_1 (not_1_out, HaltTesting);
  not not_2 (not_2_out, Done);
  Counter #(.width(10), .max('h3ff), .ongoal("stay")) u_TestNumber (
    .count(and_1_out), .Q(TestNumber), .clk(CLK));  // open: load, D, carry, clr
  and and_1 (and_1_out, not_1_out, Ready, not_2_out);
  ROM #(.addrWidth(10), .dataWidth(21)) rom_1 (
    .addr(TestNumber), .data({Done, Read, Write, Address, Value}));  // open: sel

  // Notes on the sheet:
  //   contents of rom_1 (hex, n*v repeats v):
  //   40005 40106 40307 40308 41009 4110a 4130b 4130c 4200d 4210e 4230f 42310 43011 43112 43313 43314
  //   44015 44116 44317 44318 45019 4511a 4531b 4531c 80000 80100 80300 80300 81000 81100 81300 81300
  //   82000 82100 82300 82300 83000 83100 83300 83300 84000 84100 84300 84300 85000 85100 85300 85300 0
  //   100000
endmodule

module Checker (
  input  [9:0] TestNumber,
  input  [7:0] YourByteRead,
  output CmdIsRead,
  output [7:0] CorrectByteRead,
  output Correct
);

  wire comparator_1_eq;
  wire [9:0] subtractor_1_out;

  // Probe on TestNumber
  Subtractor #(.width(10)) subtractor_1 (.a(TestNumber), .b(10'h1), .out(subtractor_1_out));  // open: bin, bout
  ROM #(.addrWidth(10), .dataWidth(9)) rom_1 (
    .addr(subtractor_1_out), .data({CmdIsRead, CorrectByteRead}));  // open: sel
  Comparator #(.mode("unsigned")) comparator_1 (
    .a(YourByteRead), .b(CorrectByteRead), .eq(comparator_1_eq));  // open: gt, lt
  and and_1 (Correct, comparator_1_eq, CmdIsRead);

  // Other names for the same wires on the sheet: Test_Number[9:0] = TestNumber

  // Notes on the sheet:
  //   Read Solutions
  //   contents of rom_1 (hex, n*v repeats v):
  //   5 6 7 8 9 a b c d e f 10 11 12 13 14 15 16 17 18 19 1a 1b 1c 105 106 108 108 109 10a 10c 10c 10d 10e
  //   110 110 111 112 114 114 115 116 118 118 119 11a 11c 11c
endmodule

module Line (
  input  UpdateTag,
  input  UpdateDirtyBit,
  input  UpdateValid,
  input  UpdateAge,
  input  [1:0] Offset,
  input  CLK,
  input  [7:0] ValueIn,
  input  WriteToVal,
  output [6:0] TagOut,
  output DirtyBitOut,
  output ValidOut,
  output [1:0] AgeOut,
  output [7:0] ValueOut
);

  wire bit_extender_2_out, bit_extender_3_out, WriteToVal0, WriteToVal1, WriteToVal2, WriteToVal3;
  wire [1:0] bit_extender_4_out;
  wire [6:0] bit_extender_1_out;
  wire [7:0] Val0, Val1, Val2, Val3;

  Demultiplexer #(.select(2), .enable("false")) demultiplexer_1 (
    .out0(WriteToVal0), .out1(WriteToVal1), .out2(WriteToVal2), .out3(WriteToVal3), .in(WriteToVal),
    .sel(Offset));
  Bit_Extender #(.out_width(7)) bit_extender_1 (.in(ValueIn), .out(bit_extender_1_out));
  Register #(.width(7)) register_1 (.D(bit_extender_1_out), .en(UpdateTag), .Q(TagOut), .clk(CLK));  // open: clr
  Bit_Extender #(.out_width(1)) bit_extender_2 (.in(ValueIn), .out(bit_extender_2_out));
  Register #(.width(1)) register_2 (
    .D(bit_extender_2_out), .en(UpdateDirtyBit), .Q(DirtyBitOut), .clk(CLK));  // open: clr
  Bit_Extender #(.out_width(1)) bit_extender_3 (.in(ValueIn), .out(bit_extender_3_out));
  Register #(.width(1)) register_3 (.D(bit_extender_3_out), .en(UpdateValid), .Q(ValidOut), .clk(CLK));  // open: clr
  Bit_Extender #(.out_width(2)) bit_extender_4 (.in(ValueIn), .out(bit_extender_4_out));
  Register #(.width(2)) register_4 (.D(bit_extender_4_out), .en(UpdateAge), .Q(AgeOut), .clk(CLK));  // open: clr
  Register u_Val0 (.en(WriteToVal0), .Q(Val0), .clk(CLK));  // open: D, clr
  Register u_Val1 (.en(WriteToVal1), .Q(Val1), .clk(CLK));  // open: D, clr
  Register u_Val2 (.en(WriteToVal2), .Q(Val2), .clk(CLK));  // open: D, clr
  Register u_Val3 (.en(WriteToVal3), .Q(Val3), .clk(CLK));  // open: D, clr
  Multiplexer #(.select(2), .width(8), .enable("false")) multiplexer_1 (
    .in0(Val0), .in1(Val1), .in2(Val2), .in3(Val3), .out(ValueOut), .sel(Offset));

  // Notes on the sheet:
  //   Scroll below!!!!
  //   Depends on FSM
  //   Write To Each Val (ONE at a time) When Scanning From Mem
  //   POINTS:
  //   (3) Line can accept NO MORE than 8 bits per cycle
  //   (1) IDEA For ValueIn: Just have no more than 1 data register update PER CYCLE
  //   (2) Either ValueIn Feeds into Tag, DirtyBit, Valid, Age, Val0, Val1, Val2, or Val3
  //   Line returns currently stored Tag, Dirty Bit, Valid, and Age Data
  //   Based on Offset, return the correct Value
endmodule

module nextAge (
  input  Set,
  input  Set_2
);

  Multiplexer #(.select(2), .width(7), .enable("false")) multiplexer_1 ();  // open: in0, in1, in2, in3, out, sel
endmodule

module Set (
  input  [6:0] Tag,
  input  [1:0] Offset,
  input  CLK,
  input  Read,
  input  Write
);

  wire UpdateDirtyBit, UpdateTag, UpdateValid;
  wire [1:0] OffsetToLine0, OffsetToLine1, OffsetToLine2;
  wire [2:0] State_s__Where_We_Select_Which_Bit_To_Update;

  Demultiplexer #(.select(3), .width(2), .enable("false")) demultiplexer_1 (
    .out0(OffsetToLine0), .out1(OffsetToLine1), .out2(OffsetToLine2), .in(Offset), .sel(3'b000));  // open: out3, out4, out5, out6, out7
  Demultiplexer #(.select(3), .enable("false")) demultiplexer_2 (
    .in(1'b0), .sel(State_s__Where_We_Select_Which_Bit_To_Update));  // open: out0, out1, out2, out3, out4, out5, out6, out7
  Line Line0 (
    .UpdateTag(UpdateTag), .UpdateDirtyBit(UpdateDirtyBit), .UpdateValid(UpdateValid),
    .Offset(OffsetToLine0), .CLK(CLK));  // open: UpdateAge, ValueIn, WriteToVal, TagOut, DirtyBitOut, ValidOut, AgeOut, ValueOut
  Line Line1 (
    .UpdateTag(UpdateTag), .UpdateDirtyBit(UpdateDirtyBit), .UpdateValid(UpdateValid),
    .Offset(OffsetToLine1), .CLK(CLK));  // open: UpdateAge, ValueIn, WriteToVal, TagOut, DirtyBitOut, ValidOut, AgeOut, ValueOut
  Line Line2 (
    .UpdateTag(UpdateTag), .UpdateDirtyBit(UpdateDirtyBit), .UpdateValid(UpdateValid),
    .Offset(OffsetToLine2), .CLK(CLK));  // open: UpdateAge, ValueIn, WriteToVal, TagOut, DirtyBitOut, ValidOut, AgeOut, ValueOut

  // Notes on the sheet:
  //   (1) This DMX helps us search through each Set for Tag
  //   (2) This DMX updates the following dirty bits PER cycle
  //   (3) FSM Goes Here?
  //   For Each Set, There are 3 Lines
  //   Maybe compare the tag output to the tag input?
  //   (From the line I mean)
endmodule
